# Fritzing sketch ESP32-CAM_part (saved by Fritzing 0.9.3b)
breadboards: 1

parts:
  ESP32_-_Back1 = ESP32 - CAM
  부품1 = FTDI Basic Programmer

nets:
  N1: ESP32_-_Back1.3.3V, 부품1.POWER
  N2: ESP32_-_Back1.GPIO0, ESP32_-_Back1.GND#12
  N3: ESP32_-_Back1.GPIO3_/_RX, 부품1.TXO
  N4: ESP32_-_Back1.GPIO1_/_TX, 부품1.RXI
  N5: ESP32_-_Back1.GND#16, 부품1.GND

custom parts:
  ESP32 - CAM: The ESP32-CAM has a very competitive small-size camera module that can operate independently as a minimum system with a footprint of only 27*40.5*4.5mm and a deep sleep current of up to 6mA.
